# Fritzing sketch ESQUEMA_LIVRO_SONORO (saved by Fritzing 0.9.3b)
breadboards: 1

parts:
  Part1 = Arduino Uno (Rev3)
  R1 = Photocell (LDR) [package=THT]
  R2 = Resistor [tolerance=±5% resistance=220 package=THT]
  Part2 = Arduino MP3 Player Shield
  LED1 = LED - 3mm [color="Red (633nm)" package="3 mm [THT]"]

nets:
  N1: Part1.A0, R1.pin_0, R2.Pin_1
  N2: Part1.5V, R1.pin_1
  N3: Part1.GND, R2.Pin_0
  N4: Part2.5V-SCK, LED1.anode
  N5: Part2.GND, LED1.cathode
